// Logisim project CBRLAB4.circ as structural Verilog: 9 circuits, main circuit main
module Half_Adder (
  input  A,
  input  B,
  output SUM,
  output Carry
);

  xor xor_1 (SUM, A, B);
  and and_1 (Carry, A, B);
endmodule

module Full_Adder (
  input  in_1,
  input  in_2,
  input  in_3,
  output out_4,
  output out_5
);

  wire Half_Adder_2_carry, Half_Adder_carry, Half_Adder_sum;

  Half_Adder Half_Adder (.A(in_2), .B(in_3), .SUM(Half_Adder_sum), .Carry(Half_Adder_carry));
  Half_Adder Half_Adder_2 (.A(in_1), .B(Half_Adder_sum), .SUM(out_4), .Carry(Half_Adder_2_carry));
  or or_1 (out_5, Half_Adder_2_carry, Half_Adder_carry);
endmodule

module _4_Bit_Adder_by_FA (
  input  in_1,
  input  in_2,
  input  in_3,
  input  in_4,
  input  in_5,
  input  in_6,
  input  in_7,
  input  in_8,
  output out_9,
  output out_10,
  output out_11,
  output out_12,
  output out_13
);

  wire full_adder_2_out_5, full_adder_3_out_5, full_adder_4_out_5;

  Full_Adder full_adder_1 (.in_2(in_1), .in_3(in_5), .in_1(full_adder_2_out_5), .out_4(out_10), .out_5(out_9));
  Full_Adder full_adder_2 (
    .in_2(in_2), .in_3(in_6), .in_1(full_adder_3_out_5), .out_4(out_11), .out_5(full_adder_2_out_5));
  Full_Adder full_adder_3 (
    .in_2(in_3), .in_3(in_7), .in_1(full_adder_4_out_5), .out_4(out_12), .out_5(full_adder_3_out_5));
  Full_Adder full_adder_4 (.in_2(in_4), .in_3(in_8), .in_1(1'b0), .out_4(out_13), .out_5(full_adder_4_out_5));
endmodule

module _2_Bit_Adder_by_TT (
  input  in_1,
  input  in_2,
  input  in_3,
  input  in_4,
  output out_5,
  output out_6,
  output out_7
);

  f0 f0_1 (.in_1(in_2), .in_2(in_4), .out_3(out_6));
  f1 f1_1 (.in_1(in_1), .in_2(in_2), .in_3(in_3), .in_4(in_4), .out_5(out_5));
  f2 f2_1 (.in_1(in_1), .in_2(in_2), .in_3(in_3), .in_4(in_4), .out_5(out_7));
endmodule

module main (
  input  in_1,
  input  in_2,
  input  in_3,
  input  in_4,
  input  in_5,
  input  in_6,
  input  in_7,
  input  in_8,
  input  in_9,
  input  in_10,
  input  in_11,
  input  in_12,
  input  in_13,
  input  in_14,
  input  in_15,
  input  in_16,
  input  in_17,
  input  in_18,
  input  in_19,
  input  in_20,
  input  in_21,
  input  in_22,
  input  in_23,
  input  in_24,
  input  in_25,
  input  in_26,
  input  in_27,
  input  in_28,
  output out_29,
  output out_30,
  output out_31,
  output out_32,
  output out_33,
  output out_34,
  output out_35,
  output out_36,
  output out_37,
  output out_38,
  output out_39,
  output out_40,
  output out_41,
  output out_42,
  output out_43,
  output out_44,
  output out_45
);

  _4_Bit_Adder_by_FA u_4_bit_adder_by_fa_1 (
    .in_1(in_5), .in_2(in_6), .in_3(in_7), .in_4(in_8), .in_5(in_9), .in_6(in_10), .in_7(in_11),
    .in_8(in_12), .out_9(out_29), .out_10(out_30), .out_11(out_31), .out_12(out_32), .out_13(out_33));
  _8_Bit_Adder_by_FA u_8_bit_adder_by_fa_1 (
    .in_1(in_13), .in_2(in_14), .in_3(in_15), .in_4(in_16), .in_5(in_17), .in_6(in_18), .in_7(in_19),
    .in_8(in_20), .in_9(in_21), .in_10(in_22), .in_11(in_23), .in_12(in_24), .in_13(in_25), .in_14(in_26),
    .in_15(in_27), .in_16(in_28), .out_17(out_37), .out_18(out_38), .out_19(out_39), .out_20(out_40),
    .out_21(out_41), .out_22(out_42), .out_23(out_43), .out_24(out_44), .out_25(out_45));
  _2_Bit_Adder_by_TT u_2_bit_adder_by_tt_1 (
    .in_1(in_1), .in_2(in_2), .in_3(in_3), .in_4(in_4), .out_7(out_34), .out_5(out_35), .out_6(out_36));
endmodule

module f0 (
  input  in_1,
  input  in_2,
  output out_3
);

  wire and_1_out, and_2_out, not_1_out, not_2_out;

  not not_1 (not_1_out, in_2);
  not not_2 (not_2_out, in_1);
  and and_1 (and_1_out, in_1, not_1_out);
  and and_2 (and_2_out, not_2_out, in_2);
  or or_1 (out_3, and_1_out, and_2_out);
endmodule

module f1 (
  input  in_1,
  input  in_2,
  input  in_3,
  input  in_4,
  output out_5
);

  wire and_1_out, and_2_out, and_3_out, and_4_out, and_5_out, and_6_out, not_1_out, not_2_out, not_3_out,
       not_4_out, not_5_out, not_6_out, not_7_out, not_8_out, not_9_out, not_10_out;

  and and_1 (and_1_out, in_1, not_1_out, not_2_out);
  not not_1 (not_1_out, in_3);
  not not_2 (not_2_out, in_4);
  and and_2 (and_2_out, in_1, not_3_out, not_4_out);
  not not_3 (not_3_out, in_2);
  not not_4 (not_4_out, in_3);
  not not_5 (not_5_out, in_1);
  not not_6 (not_6_out, in_2);
  and and_3 (and_3_out, not_5_out, not_6_out, in_3);
  not not_7 (not_7_out, in_1);
  and and_4 (and_4_out, not_7_out, in_3, not_8_out);
  not not_8 (not_8_out, in_4);
  not not_9 (not_9_out, in_1);
  and and_5 (and_5_out, not_9_out, in_2, not_10_out, in_4);
  not not_10 (not_10_out, in_3);
  and and_6 (and_6_out, in_1, in_2, in_3, in_4);
  or or_1 (out_5, and_1_out, and_2_out, and_3_out, and_4_out, and_5_out, and_6_out);
endmodule

module f2 (
  input  in_1,
  input  in_2,
  input  in_3,
  input  in_4,
  output out_5
);

  wire and_1_out, and_2_out, and_3_out, and_4_out, and_5_out;

  and and_1 (and_1_out, in_1, in_3);
  and and_2 (and_2_out, in_1, in_3, in_4);
  and and_3 (and_3_out, in_2, in_3, in_4);
  and and_4 (and_4_out, in_1, in_2, in_3);
  and and_5 (and_5_out, in_1, in_2, in_4);
  or or_1 (out_5, and_1_out, and_2_out, and_3_out, and_4_out, and_5_out);
endmodule

module _8_Bit_Adder_by_FA (
  input  in_1,
  input  in_2,
  input  in_3,
  input  in_4,
  input  in_5,
  input  in_6,
  input  in_7,
  input  in_8,
  input  in_9,
  input  in_10,
  input  in_11,
  input  in_12,
  input  in_13,
  input  in_14,
  input  in_15,
  input  in_16,
  output out_17,
  output out_18,
  output out_19,
  output out_20,
  output out_21,
  output out_22,
  output out_23,
  output out_24,
  output out_25
);

  wire full_adder_2_out_5, full_adder_3_out_5, full_adder_4_out_5, full_adder_5_out_5, full_adder_6_out_5,
       full_adder_7_out_5, full_adder_8_out_5;

  Full_Adder full_adder_1 (.in_2(in_1), .in_3(in_9), .in_1(full_adder_2_out_5), .out_4(out_18), .out_5(out_17));
  Full_Adder full_adder_2 (
    .in_2(in_2), .in_3(in_10), .in_1(full_adder_3_out_5), .out_4(out_19), .out_5(full_adder_2_out_5));
  Full_Adder full_adder_3 (
    .in_2(in_3), .in_3(in_11), .in_1(full_adder_4_out_5), .out_4(out_20), .out_5(full_adder_3_out_5));
  Full_Adder full_adder_4 (
    .in_2(in_4), .in_3(in_12), .in_1(full_adder_5_out_5), .out_4(out_21), .out_5(full_adder_4_out_5));
  Full_Adder full_adder_5 (
    .in_2(in_5), .in_3(in_13), .in_1(full_adder_6_out_5), .out_4(out_22), .out_5(full_adder_5_out_5));
  Full_Adder full_adder_6 (
    .in_2(in_6), .in_3(in_14), .in_1(full_adder_7_out_5), .out_4(out_23), .out_5(full_adder_6_out_5));
  Full_Adder full_adder_7 (
    .in_2(in_7), .in_3(in_15), .in_1(full_adder_8_out_5), .out_4(out_24), .out_5(full_adder_7_out_5));
  Full_Adder full_adder_8 (.in_2(in_8), .in_3(in_16), .in_1(1'b0), .out_4(out_25), .out_5(full_adder_8_out_5));
endmodule
