// Logisim project LAB1.circ as structural Verilog: 5 circuits, main circuit main
module main (
  input  in_1,
  input  in_2,
  input  in_3,
  input  in_4,
  input  in_5,
  input  in_6,
  input  in_7,
  output [1:0] out_8,
  output [1:0] out_9,
  output [1:0] out_10,
  output [1:0] out_11
);

  wire clock_1_out, multiplexer_1_out;
  wire [1:0] crossing_1_state;

  Clock clock_1 (.out(clock_1_out));
  Multiplexer #(.enable("false")) multiplexer_1 (.in0(clock_1_out), .in1(in_1), .out(multiplexer_1_out), .sel(in_2));
  crossing crossing_1 (
    .Ta(in_3), .Tb(in_4), .BTa(in_5), .BTb(in_6), .State(crossing_1_state), .Clock(multiplexer_1_out),
    .RESET(in_7));
  // Probe on crossing_1_state
  Crossing_Decoder crossing_decoder_1 (.in_1(crossing_1_state), .La(out_8), .Lb(out_9), .Pa(out_10), .Pb(out_11));
endmodule

module crossing (
  input  Ta,
  input  Clock,
  input  Tb,
  input  RESET,
  input  BTa,
  input  BTb,
  output [1:0] State
);

  wire [1:0] cr_s0_1_out_3, cr_s2_1_out_3, multiplexer_1_out;

  cr_s0 cr_s0_1 (.a(Ta), .b(BTa), .out_3(cr_s0_1_out_3));
  cr_s2 cr_s2_1 (.in_1(Tb), .in_2(BTb), .out_3(cr_s2_1_out_3));
  Multiplexer #(.select(2), .width(2), .enable("false")) multiplexer_1 (
    .in0(cr_s0_1_out_3), .in1(2'b10), .in2(cr_s2_1_out_3), .in3(2'b00), .out(multiplexer_1_out), .sel(State));
  Register #(.width(2)) register_1 (.D(multiplexer_1_out), .Q(State), .clk(Clock), .clr(RESET));  // open: en
endmodule

module cr_s0 (
  input  a,
  input  b,
  output [1:0] out_3
);

  wire not_1_out;

  not not_1 (not_1_out, a);
  or or_1 (out_3[0], not_1_out, b);

  assign out_3[1] = 1'b0;
endmodule

module cr_s2 (
  input  in_1,
  input  in_2,
  output [1:0] out_3
);

  wire not_1_out;

  not not_1 (not_1_out, in_1);
  or or_1 (out_3[0], not_1_out, in_2);

  assign out_3[1] = 1'b1;
endmodule

module Crossing_Decoder (
  input  [1:0] in_1,
  output [1:0] La,
  output [1:0] Lb,
  output [1:0] Pa,
  output [1:0] Pb
);

  Multiplexer #(.select(2), .width(2), .enable("false")) multiplexer_1 (
    .in0(2'b00), .in1(2'b01), .in2(2'b10), .in3(2'b10), .out(La), .sel(in_1));
  Multiplexer #(.select(2), .width(2), .enable("false")) multiplexer_2 (
    .in0(2'b10), .in1(2'b10), .in2(2'b00), .in3(2'b01), .out(Lb), .sel(in_1));
  Multiplexer #(.select(2), .width(2), .enable("false")) multiplexer_3 (
    .in0(2'b10), .in1(2'b10), .in2(2'b00), .in3(2'b10), .out(Pa), .sel(in_1));
  Multiplexer #(.select(2), .width(2), .enable("false")) multiplexer_4 (
    .in0(2'b00), .in1(2'b10), .in2(2'b10), .in3(2'b10), .out(Pb), .sel(in_1));
endmodule
